# Fritzing sketch qtpy_compressed (saved by Fritzing 0.9.9b)
circuit board: 6.86881cm x 3.1335cm

parts:
  IC1 = Hex Inverter Schmitt Trigger SN74HC14 [package="DIP (Dual Inline)"]
  Part1 = Adafruit QT Py RP2040 [part_number="Adafruit #4900"]
  R2 = Resistor [tolerance=±5% resistance=220 power=0.25 package=THT]
  R3 = Resistor [tolerance=±5% resistance=220 power=0.25 package=THT]
  R4 = Resistor [tolerance=±5% resistance=220 power=0.25 package=THT]
  R5 = Resistor [tolerance=±5% resistance=220 power=0.25 package=THT]
  R6 = Resistor [tolerance=±5% resistance=220 power=0.25 package=THT]
  R7 = Resistor [tolerance=±5% resistance=220 power=0.25 package=THT]
  R8 = Resistor [tolerance=±5% resistance=220 power=0.25 package=THT]
  R9 = Resistor [tolerance=±5% resistance=220 power=0.25 package=THT]
  JP4 = Header 1 [package=1x01_offset]  # not connected
  JP5 = Header 1 [package=1x01_offset]
  JP6 = Header 1 [package=1x01_offset]  # not connected
  JP7 = Header 1 [package=1x01_offset]
  JP8 = Header 1 [package=1x01_offset]
  JP9 = Header 1 [package=1x01_offset]
  JP10 = Header 1 [package=1x01_offset]
  JP11 = Header 1 [package=1x01_offset]
  JP12 = Header 1 [package=1x01_offset]
  JP13 = Header 1 [package=1x01_offset]
  JP14 = Header 1 [package=1x01_offset]

nets:
  N1: IC1.1A, R4.Pin_0
  N2: IC1.1Y, Part1.A3
  N3: IC1.2A, R5.Pin_0
  N4: IC1.2Y, Part1.SCK
  GND: IC1.GND, Part1.GND, JP8.1
  N5: IC1.5Y, Part1.RX
  N6: IC1.5A, R3.Pin_0
  N7: IC1.6Y, Part1.MISO
  N8: IC1.6A, R2.Pin_0
  VCC: IC1.VCC, Part1.+3V3, R6.Pin_1, R7.Pin_1, R8.Pin_1, R9.Pin_1
  N9: Part1.A0, JP14.1
  N10: Part1.A1, JP13.1
  N11: Part1.A2, JP12.1
  N12: Part1.SDA, JP7.1
  N13: R2.Pin_1, JP11.1
  N14: R3.Pin_1, JP10.1
  N15: R4.Pin_1, JP5.1
  N16: R5.Pin_1, JP9.1

notes:
  GPIO4
  GPIO26
  GPIO5
  GPIO6

custom parts:
  Adafruit QT Py RP2040: Description What a cutie pie! Or is it... a QT Py? This diminutive dev board comes with one of our new favorite chip, the RP2040. It's been made famous in the new Raspberry Pi Pico and our Feather RP2040 and ItsyBitsy RP2040, but what if we wanted something really smol? A new chip means a new QT Py, and the Raspberry Pi RP2040 is no exception. When we saw this chip we thought "this chip is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
