# Fritzing sketch qtpy_exploded (saved by Fritzing 0.9.9b)

parts:
  Part2 = Adafruit QT Py RP2040 [part_number="Adafruit #4900"]
  IC2 = Hex Inverter Schmitt Trigger SN74HC14 [package="DIP (Dual Inline)"]
  R10 = Resistor [tolerance=±5% resistance=10k power=0.25 package=THT]
  R11 = Resistor [tolerance=±5% resistance=10k power=0.25 package=THT]
  R12 = Resistor [tolerance=±5% resistance=10k power=0.25 package=THT]
  R13 = Resistor [tolerance=±5% resistance=10k power=0.25 package=THT]
  R14 = Resistor [tolerance=±5% resistance=10k power=0.25 package=THT]
  R15 = Resistor [tolerance=±5% resistance=10k power=0.25 package=THT]
  R16 = Resistor [tolerance=±5% resistance=10k power=0.25 package=THT]
  R17 = Resistor [tolerance=±5% resistance=10k power=0.25 package=THT]
  C2 = Ceramic Capacitor [capacitance=100nF voltage=35V package="200 mil [THT, multilayer]"]
  Scroll_(Click_Right_Mouse) = Rotary Encoder with Knob
  C3 = Ceramic Capacitor [capacitance=100nF voltage=35V package="200 mil [THT, multilayer]"]
  C4 = Ceramic Capacitor [capacitance=100nF voltage=35V package="200 mil [THT, multilayer]"]
  C5 = Ceramic Capacitor [capacitance=100nF voltage=35V package="200 mil [THT, multilayer]"]
  Toot_(Left_Mouse) = Momentary Switch [package=ksa_sealed_tac_switch]
  Scale = POT [package=alps_pot]
  Invert_or_Disable = Toggle Switch [package=THT]

nets:
  +3V3: Part2.+3V3, IC2.VCC, R12.Pin_1
  N1: Part2.A0, Scale.S
  N2: Part2.A1, Scale.E
  N3: Part2.A2, Invert_or_Disable.L2
  N4: Part2.A3, IC2.1Y
  N5: Part2.SDA, Invert_or_Disable.L1
  N6: Part2.RX, IC2.5Y
  N7: Part2.SCK, IC2.2Y
  N8: Part2.MISO, IC2.6Y
  N9: Part2.GND, C3.0, Scale.A
  N10: IC2.1A, R15.Pin_0, C4.0
  N11: IC2.2A, R17.Pin_0, C5.1
  N12: IC2.5A, R13.Pin_1, C2.0
  N13: IC2.6A, R11.Pin_0, C3.1
  N14: R10.Pin_0, R13.Pin_0, Scroll_(Click_Right_Mouse).no_name_yet#1
  N15: R11.Pin_1, R16.Pin_0, Scroll_(Click_Right_Mouse).no_name_yet#5
  N16: R12.Pin_0, R15.Pin_1, Toot_(Left_Mouse).1
  N17: R14.Pin_0, R17.Pin_1, Scroll_(Click_Right_Mouse).no_name_yet#3

notes:
  GPIO4
  GPIO26
  GPIO5
  GPIO6

custom parts:
  Adafruit QT Py RP2040: Description What a cutie pie! Or is it... a QT Py? This diminutive dev board comes with one of our new favorite chip, the RP2040. It's been made famous in the new Raspberry Pi Pico and our Feather RP2040 and ItsyBitsy RP2040, but what if we wanted something really smol? A new chip means a new QT Py, and the Raspberry Pi RP2040 is no exception. When we saw this chip we thought "this chip is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
  Rotary Encoder with Knob: Rotary Encoder with 1/4" Shaft and Knob
